// Logisim project Datapath.circ as structural Verilog: 1 circuit, main circuit datapath
module datapath (
);

  wire [31:0] meminstr_1_instruction;

  MemInstr meminstr_1 (.Instruction(meminstr_1_instruction));  // open: PC_address
  // Decoder decoder_1: pin names not known; wires that end beside it: meminstr_1_instruction
  // ControllerUnity controllerunity_1: pin names not known
  // RegisterFile registerfile_1: pin names not known
  // ULAControllerUnity ulacontrollerunity_1: pin names not known
  // ULA_main main_1: pin names not known
  // datamem datamem_1: pin names not known
endmodule
